# Fritzing sketch sketch (saved by Fritzing 0.9.2b)
circuit board: 8.46667cm x 5.64444cm
breadboards: 1

parts:
  U1 = NodeMCU V3.0
  DHT1 = DHT22 Humidity and Temperature Sensor
  R1 = Resistor [tolerance=±5% resistance=1k package=THT]
  R2 = Resistor [tolerance=±5% resistance=220 package=THT]
  R3 = Resistor [tolerance=±5% resistance=220 package=THT]
  R4 = Resistor [tolerance=±5% resistance=220 package=THT]
  R5 = Resistor [tolerance=±5% resistance=220 package=THT]
  R6 = Resistor [tolerance=±5% resistance=220 package=THT]
  C1 = Electrolytic Capacitor [capacitance=4.7µF voltage=50V package="0605 [SMD, electrolytic]"]
  C2 = Electrolytic Capacitor [capacitance=4.7µF voltage=50V package="0605 [SMD, electrolytic]"]
  C3 = Electrolytic Capacitor [capacitance=4.7µF voltage=50V package="0605 [SMD, electrolytic]"]
  C4 = Electrolytic Capacitor [capacitance=4.7µF voltage=50V package="0605 [SMD, electrolytic]"]
  C5 = Electrolytic Capacitor [capacitance=4.7µF voltage=50V package="0605 [SMD, electrolytic]"]
  S1 = Momentary Switch [package=ksa_sealed_tac_switch]
  S2 = Momentary Switch [package=ksa_sealed_tac_switch]
  S3 = Momentary Switch [package=ksa_sealed_tac_switch]
  S4 = Momentary Switch [package=ksa_sealed_tac_switch]
  S5 = Momentary Switch [package=ksa_sealed_tac_switch]

nets:
  N1: U1.D1, R5.Pin_0, C1.-, S1.1, S1.3
  N2: U1.D2, R6.Pin_0, C2.-, S2.1, S2.3
  N3: U1.D4, R2.Pin_0, C3.-, S3.1, S3.3
  3V3: U1.3V3, DHT1.VDD, R1.Pin_0, R2.Pin_1, R3.Pin_1, R4.Pin_1, R5.Pin_1, R6.Pin_1, C1.+, C2.+, C3.+, C4.+, C5.+
  GND: U1.GND, DHT1.GND, S1.2, S1.4, S2.2, S2.4, S3.2, S3.4, S4.2, S4.4, S5.2, S5.4
  N4: U1.D5, R3.Pin_0, C5.-, S5.1, S5.3
  N5: U1.D6, DHT1.DATA, R1.Pin_1
  N6: U1.D7, R4.Pin_0, C4.-, S4.1, S4.3

custom parts:
  NodeMCU V3.0: ESP8266 based NodeMCU
